# Fritzing sketch Control Board (saved by Fritzing 0.9.3b)
circuit board: 6.01882cm x 13cm
breadboards: 1

parts:
  J4 = shrouded pin header, 30 pins [form="♂ (shrouded male)"]
  C2 = shrouded pin header, 30 pins [form="♂ (shrouded male)"]
  Part2 = Arduino Mega ADK (Rev3)

nets:
  N1: J4.pin1, Part2.D15/RX3
  N2: J4.pin2, Part2.D19/RX1
  N3: J4.pin3, Part2.A1
  N4: J4.pin4, Part2.A0
  N5: J4.pin5, Part2.A7
  N6: J4.pin6, Part2.A6
  N7: J4.pin7, Part2.D48
  N8: J4.pin8, Part2.D46
  N9: J4.pin9, Part2.D9_PWM
  N10: J4.pin18, Part2.D29
  N11: J4.pin30, Part2.D2_PWM
  N12: C2.pin3, C2.pin28, Part2.VIN
  N13: C2.pin25, Part2.D52/SCK
  N14: C2.pin26, Part2.D51/MOSI
  N15: C2.pin27, Part2.D50/MISO

notes:
  Connector 1
  Connector 2
