# Fritzing sketch Custom Board (saved by Fritzing 0.9.3b)
circuit board: 8.5cm x 20cm
breadboards: 1

parts:
  J1 = shrouded pin header, 40 pins [form="♂ (shrouded male)"]
  J5 = Generic female header - 2 pins [form="♀ (female)" package=THT]
  J6 = Generic female header - 2 pins [form="♀ (female)" package=THT]
  J7 = Generic female header - 2 pins [form="♀ (female)" package=THT]
  J4 = Generic female header - 2 pins [form="♀ (female)" package=THT]
  J9 = shrouded pin header, 40 pins [form="♂ (shrouded male)"]  # not connected
  J8 = molex pin header, 2 pins [form=molex]
  WeMos_D1_Mini_Micro_SD_Shield1 = WeMos D1 Mini Micro SD Shield  # not connected
  J19 = shrouded pin header, 40 pins [form="♂ (shrouded male)"]  # not connected
  OMRON2 = OMRON PCB Power Relay – G5LE [part_number="G5LE-1\n" package=THT]  # not connected
  OMRON3 = OMRON PCB Power Relay – G5LE [part_number="G5LE-1\n" package=THT]  # not connected
  Q2 = Basic FET N-Channel [package="TO220 [THT]"]  # not connected
  OMRON4 = OMRON PCB Power Relay – G5LE [part_number="G5LE-1\n" package=THT]  # not connected
  J21 = Generic female header - 2 pins [form="♀ (female)" package=THT]
  J22 = Generic female header - 2 pins [form="♀ (female)" package=THT]
  J23 = Generic female header - 2 pins [form="♀ (female)" package=THT]
  J25 = Generic female header - 2 pins [form="♀ (female)" package=THT]
  Q3 = Basic FET N-Channel [package="TO220 [THT]"]  # not connected
  Q4 = Basic FET N-Channel [package="TO220 [THT]"]  # not connected
  Q5 = Basic FET N-Channel [package="TO220 [THT]"]  # not connected
  Q6 = Basic FET N-Channel [package="TO220 [THT]"]  # not connected
  Q7 = Basic FET N-Channel [package="TO220 [THT]"]  # not connected
  J24 = shrouded pin header, 40 pins [form="♂ (shrouded male)"]

nets:
  N1: J1.pin1, J1.pin40, J4.pin2, J4.pin_11
  N2: J1.pin2, J1.pin39, J4.pin_3, J4.pin_10
  N3: J1.pin3, J1.pin38, J4.pin_4, J4.pin_9
  N4: J1.pin4, J1.pin37, J4.pin_5, J4.pin_8
  N5: J1.pin5, J1.pin36, J6.pin2, J6.pin_11
  N6: J1.pin6, J1.pin35, J6.pin_3, J6.pin_10
  N7: J1.pin7, J1.pin34, J6.pin_4, J6.pin_9
  N8: J1.pin8, J1.pin33, J6.pin_5, J6.pin_8
  N9: J1.pin9, J1.pin32, J7.pin2, J7.pin_11
  N10: J1.pin10, J1.pin31, J7.pin_3, J7.pin_10
  N11: J1.pin11, J1.pin30, J7.pin_4, J7.pin_9
  N12: J1.pin12, J1.pin29, J7.pin_5, J7.pin_8
  N13: J1.pin13, J1.pin28, J5.pin2, J5.pin_11
  N14: J1.pin14, J1.pin27, J5.pin_3, J5.pin_10
  N15: J1.pin15, J1.pin26, J5.pin_4, J5.pin_9
  N16: J1.pin16, J1.pin25, J5.pin_5, J5.pin_8
  N17: J1.pin17, J1.pin19, J1.pin21, J1.pin23
  N18: J5.pin1, J5.pin_12, J6.pin1, J6.pin_12, J7.pin1, J7.pin_12, J4.pin1, J4.pin_12, J8.pin2, J21.pin1, J21.pin_12, J22.pin1, J22.pin_12, J23.pin1, J23.pin_12, J25.pin1, J25.pin_12
  N19: J5.pin_17, J6.pin_17, J7.pin_17, J4.pin_17
  N20: J5.pin_18, J6.pin_18, J7.pin_18, J4.pin_18
  N21: J5.pin_19, J6.pin_19, J7.pin_19, J4.pin_19
  N22: J5.pin_20, J6.pin_20, J7.pin_20, J4.pin_20
  N23: J6.pin_15, J7.pin_15
  N24: J6.pin_16, J7.pin_16
  N25: J21.pin2, J21.pin_11, J24.pin9, J24.pin32
  N26: J21.pin_3, J21.pin_10, J24.pin10, J24.pin31
  N27: J21.pin_4, J21.pin_9, J24.pin11, J24.pin30
  N28: J21.pin_5, J21.pin_8, J24.pin12, J24.pin29
  N29: J21.pin_15, J22.pin_15
  N30: J21.pin_16, J22.pin_16
  N31: J21.pin_17, J22.pin_17, J23.pin_17, J25.pin_17
  N32: J21.pin_18, J22.pin_18, J23.pin_18, J25.pin_18
  N33: J21.pin_19, J22.pin_19, J23.pin_19, J25.pin_19
  N34: J21.pin_20, J22.pin_20, J23.pin_20, J25.pin_20
  N35: J22.pin2, J22.pin_11, J24.pin5, J24.pin36
  N36: J22.pin_3, J22.pin_10, J24.pin6, J24.pin35
  N37: J22.pin_4, J22.pin_9, J24.pin7, J24.pin34
  N38: J22.pin_5, J22.pin_8, J24.pin8, J24.pin33
  N39: J23.pin2, J23.pin_11, J24.pin13, J24.pin28
  N40: J23.pin_3, J23.pin_10, J24.pin14, J24.pin27
  N41: J23.pin_4, J23.pin_9, J24.pin15, J24.pin26
  N42: J23.pin_5, J23.pin_8, J24.pin16, J24.pin25
  N43: J25.pin2, J25.pin_11, J24.pin1, J24.pin40
  N44: J25.pin_3, J25.pin_10, J24.pin2, J24.pin39
  N45: J25.pin_4, J25.pin_9, J24.pin3, J24.pin38
  N46: J25.pin_5, J25.pin_8, J24.pin4, J24.pin37
  N47: J24.pin17, J24.pin19, J24.pin21, J24.pin23

notes:
  X
  Y2
  Y1
  Z
  24v In
  Machine Connection
  Arduino
  -
  +
  GND
  EN/CS
  STEP
  DIR
  +VCC
  +VMOT
  Driver
  2211
  Miso
  Mosi
  SCK

custom parts:
  Generic female header - 2 pins: Generic female header
