# Fritzing sketch Ethernet Board (saved by Fritzing 0.9.3b)
circuit board: 9.46604cm x 4.04665cm
breadboards: 1

parts:
  U2 = RJ45 Jack [package=rj45-8]
  U3 = RJ45 Jack [package=rj45-8]
  U4 = RJ45 Jack [package=rj45-8]
  U1 = RJ45 Jack [package=rj45-8]
  J1 = shrouded pin header, 40 pins [form="♂ (shrouded male)"]

nets:
  N1: U2.3, J1.pin22
  N2: U2.4, J1.pin7, J1.pin34
  N3: U2.5, J1.pin8, J1.pin33
  N4: U2.6, J1.pin21
  N5: U2.7, J1.pin5, J1.pin36
  N6: U2.8, J1.pin6, J1.pin35
  N7: U3.4, J1.pin11, J1.pin30
  N8: U3.5, J1.pin12, J1.pin29
  N9: U3.7, J1.pin9, J1.pin32
  N10: U3.8, J1.pin10, J1.pin31
  N11: U4.3, J1.pin24
  N12: U4.4, J1.pin15, J1.pin26
  N13: U4.5, J1.pin16, J1.pin25
  N14: U4.6, J1.pin23
  N15: U4.7, J1.pin13, J1.pin28
  N16: U4.8, J1.pin14, J1.pin27
  N17: U1.1, J1.pin20
  N18: U1.2, J1.pin19
  N19: U1.3, J1.pin17
  N20: U1.4, J1.pin3, J1.pin38
  N21: U1.5, J1.pin4, J1.pin37
  N22: U1.6, J1.pin18
  N23: U1.7, J1.pin1, J1.pin40
  N24: U1.8, J1.pin2, J1.pin39

notes:
  Machine Connection
  X
  Z
  Y1
  Y2
