# Fritzing sketch Plasma Board Test (saved by Fritzing 0.9.3b)
circuit board: 20.2367cm x 8.40729cm
breadboards: 1

parts:
  J6 = shrouded pin header, 30 pins [form="♂ (shrouded male)"]  # not connected
  J7 = shrouded pin header, 30 pins [form="♂ (shrouded male)"]  # not connected
  Q8 = Basic FET N-Channel [package="TO220 [THT]"]  # not connected
  Q9 = Basic FET N-Channel [package="TO220 [THT]"]  # not connected
  Q10 = Basic FET N-Channel [package="TO220 [THT]"]  # not connected
  Q11 = Basic FET N-Channel [package="TO220 [THT]"]  # not connected
  Q12 = Basic FET N-Channel [package="TO220 [THT]"]  # not connected
  Q13 = Basic FET N-Channel [package="TO220 [THT]"]  # not connected
  WeMos_D1_Mini_Micro_SD_Shield2 = WeMos D1 Mini Micro SD Shield  # not connected
  J26 = molex pin header, 2 pins [form=molex]
  J27 = Generic female header - 2 pins [form="♀ (female)" package=THT]
  J28 = Generic female header - 2 pins [form="♀ (female)" package=THT]
  J29 = Generic female header - 2 pins [form="♀ (female)" package=THT]
  J30 = Generic female header - 2 pins [form="♀ (female)" package=THT]
  J31 = Generic female header - 2 pins [form="♀ (female)" package=THT]
  J32 = Generic female header - 2 pins [form="♀ (female)" package=THT]
  J33 = shrouded pin header, 40 pins [form="♂ (shrouded male)"]
  J34 = shrouded pin header, 40 pins [form="♂ (shrouded male)"]
  J35 = Generic female header - 2 pins [form="♀ (female)" package=THT]
  J36 = Generic female header - 2 pins [form="♀ (female)" package=THT]
  OMRON1 = OMRON PCB Power Relay – G5LE [part_number="G5LE-1\n" package=THT]  # not connected
  OMRON2 = OMRON PCB Power Relay – G5LE [part_number="G5LE-1\n" package=THT]  # not connected
  OMRON3 = OMRON PCB Power Relay – G5LE [part_number="G5LE-1\n" package=THT]  # not connected

nets:
  N1: J26.pin2, J27.pin1, J27.pin_12, J28.pin1, J28.pin_12, J29.pin1, J29.pin_12, J30.pin1, J30.pin_12, J31.pin1, J31.pin_12, J32.pin1, J32.pin_12, J35.pin1, J35.pin_12, J36.pin1, J36.pin_12
  N2: J27.pin2, J27.pin_11, J33.pin9, J33.pin32
  N3: J27.pin_3, J27.pin_10, J33.pin10, J33.pin31
  N4: J27.pin_4, J27.pin_9, J33.pin11, J33.pin30
  N5: J27.pin_5, J27.pin_8, J33.pin12, J33.pin29
  N6: J27.pin_15, J29.pin_15
  N7: J27.pin_16, J29.pin_16
  N8: J27.pin_17, J29.pin_17, J31.pin_17, J35.pin_17
  N9: J27.pin_18, J29.pin_18, J31.pin_18, J35.pin_18
  N10: J27.pin_19, J29.pin_19, J31.pin_19, J35.pin_19
  N11: J27.pin_20, J29.pin_20, J31.pin_20, J35.pin_20
  N12: J28.pin2, J28.pin_11, J34.pin9, J34.pin32
  N13: J28.pin_3, J28.pin_10, J34.pin10, J34.pin31
  N14: J28.pin_4, J28.pin_9, J34.pin11, J34.pin30
  N15: J28.pin_5, J28.pin_8, J34.pin12, J34.pin29
  N16: J28.pin_15, J30.pin_15
  N17: J28.pin_16, J30.pin_16
  N18: J28.pin_17, J30.pin_17, J32.pin_17, J36.pin_17
  N19: J28.pin_18, J30.pin_18, J32.pin_18, J36.pin_18
  N20: J28.pin_19, J30.pin_19, J32.pin_19, J36.pin_19
  N21: J28.pin_20, J30.pin_20, J32.pin_20, J36.pin_20
  N22: J29.pin2, J29.pin_11, J33.pin5, J33.pin36
  N23: J29.pin_3, J29.pin_10, J33.pin6, J33.pin35
  N24: J29.pin_4, J29.pin_9, J33.pin7, J33.pin34
  N25: J29.pin_5, J29.pin_8, J33.pin8, J33.pin33
  N26: J30.pin2, J30.pin_11, J34.pin5, J34.pin36
  N27: J30.pin_3, J30.pin_10, J34.pin6, J34.pin35
  N28: J30.pin_4, J30.pin_9, J34.pin7, J34.pin34
  N29: J30.pin_5, J30.pin_8, J34.pin8, J34.pin33
  N30: J31.pin2, J31.pin_11, J33.pin13, J33.pin28
  N31: J31.pin_3, J31.pin_10, J33.pin14, J33.pin27
  N32: J31.pin_4, J31.pin_9, J33.pin15, J33.pin26
  N33: J31.pin_5, J31.pin_8, J33.pin16, J33.pin25
  N34: J32.pin2, J32.pin_11, J34.pin13, J34.pin28
  N35: J32.pin_3, J32.pin_10, J34.pin14, J34.pin27
  N36: J32.pin_4, J32.pin_9, J34.pin15, J34.pin26
  N37: J32.pin_5, J32.pin_8, J34.pin16, J34.pin25
  N38: J33.pin1, J33.pin40, J35.pin2, J35.pin_11
  N39: J33.pin2, J33.pin39, J35.pin_3, J35.pin_10
  N40: J33.pin3, J33.pin38, J35.pin_4, J35.pin_9
  N41: J33.pin4, J33.pin37, J35.pin_5, J35.pin_8
  N42: J33.pin17, J33.pin19, J33.pin21, J33.pin23
  N43: J34.pin1, J34.pin40, J36.pin2, J36.pin_11
  N44: J34.pin2, J34.pin39, J36.pin_3, J36.pin_10
  N45: J34.pin3, J34.pin38, J36.pin_4, J36.pin_9
  N46: J34.pin4, J34.pin37, J36.pin_5, J36.pin_8
  N47: J34.pin17, J34.pin19, J34.pin21, J34.pin23

notes:
  SCK
  Mosi
  Miso
  2211
  Driver
  +VCC
  DIR
  STEP
  EN/CS
  GND
  -
  Y2
  Y1
  Machine Connection
  24v In
  Z
  X
  +VMOT

custom parts:
  Generic female header - 2 pins: Generic female header
