# Fritzing sketch Plasma Board V2 (saved by Fritzing 0.9.3b)
circuit board: 12.7055cm x 8.53721cm
breadboards: 1

parts:
  J6 = shrouded pin header, 30 pins [form="♂ (shrouded male)"]  # not connected
  J7 = shrouded pin header, 30 pins [form="♂ (shrouded male)"]  # not connected
  J9 = molex pin header, 2 pins [form=molex]
  J10 = Generic female header - 2 pins [form="♀ (female)" package=THT]
  J11 = Generic female header - 2 pins [form="♀ (female)" package=THT]
  J13 = shrouded pin header, 40 pins [form="♂ (shrouded male)"]
  J14 = Generic female header - 2 pins [form="♀ (female)" package=THT]
  J17 = molex pin header, 6 pins [form=molex]  # not connected
  J20 = shrouded pin header, 10 pins [form="♂ (shrouded male)"]  # not connected
  OMRON1 = OMRON PCB Power Relay – G5LE [part_number="G5LE-1\n" package=THT]
  J12 = Generic female header - 2 pins [form="♀ (female)" package=THT]
  D1 = Diode [package=diode-1n4001]
  J22 = screw terminal, 2 pins
  J24 = female pin header, 3 pins [form="♀ (female)"]  # not connected
  J23 = female pin header, 3 pins [form="♀ (female)"]  # not connected

nets:
  N1: J9.pin2, J10.pin1, J10.pin_12, J11.pin1, J11.pin_12, J14.pin1, J14.pin_12, J12.pin1, J12.pin_12
  N2: J10.pin2, J10.pin_11, J13.pin9, J13.pin32
  N3: J10.pin_3, J10.pin_10, J13.pin10, J13.pin31
  N4: J10.pin_4, J10.pin_9, J13.pin11, J13.pin30
  N5: J10.pin_5, J10.pin_8, J13.pin12, J13.pin29
  N6: J10.pin_16, J11.pin_16
  N7: J10.pin_17, J11.pin_17, J14.pin_17, J12.pin_17
  N8: J10.pin_18, J11.pin_18, J14.pin_18, J12.pin_18
  N9: J10.pin_19, J11.pin_19, J14.pin_19, J12.pin_19
  N10: J10.pin_20, J11.pin_20, J14.pin_20, J12.pin_20
  N11: J11.pin2, J11.pin_11, J13.pin5, J13.pin36
  N12: J11.pin_3, J11.pin_10, J13.pin4, J13.pin6, J13.pin35, J13.pin37, J14.pin_5, J14.pin_8
  N13: J11.pin_4, J11.pin_9, J13.pin7, J13.pin34
  N14: J11.pin_5, J11.pin_8, J13.pin8, J13.pin33
  N15: J13.pin1, J13.pin40, J14.pin2, J14.pin_11
  N16: J13.pin2, J13.pin39, J14.pin_3, J14.pin_10
  N17: J13.pin3, J13.pin38, J14.pin_4, J14.pin_9
  N18: J13.pin13, J13.pin28, J12.pin2, J12.pin_11
  N19: J13.pin14, J13.pin27, J12.pin_3, J12.pin_10
  N20: J13.pin15, J13.pin26, J12.pin_4, J12.pin_9
  N21: J13.pin16, J13.pin25, J12.pin_5, J12.pin_8
  N22: J13.pin17, J13.pin19, J13.pin21, J13.pin23
  N23: OMRON1.A, D1.C
  N24: OMRON1.C, J22.pin1
  N25: OMRON1.B, D1.A, J22.pin2

notes:
  SCK
  Mosi
  Miso
  2211
  Driver
  GND
  +VMOT
  +VCC
  DIR
  EN/CS
  STEP
  -
  Machine Connection
  24v In
  Z
  Y1
  Y2
  X
  Torch Height Control

custom parts:
  Generic female header - 2 pins: Generic female header
