# Fritzing sketch Plasma Board (saved by Fritzing 0.9.3b)
circuit board: 10.285cm x 12.7169cm
breadboards: 1

parts:
  J1 = shrouded pin header, 40 pins [form="♂ (shrouded male)"]
  J5 = Generic female header - 2 pins [form="♀ (female)" package=THT]
  J6 = Generic female header - 2 pins [form="♀ (female)" package=THT]
  J7 = Generic female header - 2 pins [form="♀ (female)" package=THT]
  J4 = Generic female header - 2 pins [form="♀ (female)" package=THT]
  R1 = Resistor [tolerance=±5% resistance=220 package=THT]
  R2 = Resistor [tolerance=±5% resistance=220 package=THT]
  R3 = Resistor [tolerance=±5% resistance=220 package=THT]
  R4 = Resistor [tolerance=±5% resistance=220 package=THT]
  J2 = shrouded pin header, 10 pins [form="♂ (shrouded male)"]
  J8 = molex pin header, 2 pins [form=molex]
  OMRON1 = OMRON PCB Power Relay – G5LE [part_number="G5LE-1\n" package=THT]
  J10 = molex pin header, 2 pins [form=molex]
  Q1 = NPN-Transistor [package="TO92 [THT]"]
  D1 = Zener Diode [part_number=1N4732A breakdown_voltage=3.6V package="300 mil [THT]"]
  J17 = female pin header, 3 pins [form="♀ (female)"]
  J18 = female pin header, 3 pins [form="♀ (female)"]
  R5 = Resistor [tolerance=±5% resistance=220 package=THT]
  J12 = molex pin header, 6 pins [form=molex]
  J19 = shrouded pin header, 30 pins [form="♂ (shrouded male)"]
  J20 = shrouded pin header, 30 pins [form="♂ (shrouded male)"]
  J21 = female pin header, 2 pins [form="♀ (female)"]  # not connected
  J22 = female pin header, 2 pins [form="♀ (female)"]  # not connected
  J23 = female pin header, 2 pins [form="♀ (female)"]
  J24 = female pin header, 2 pins [form="♀ (female)"]

nets:
  N1: J1.pin1, J1.pin40, J4.pin2, J4.pin_11
  N2: J1.pin2, J1.pin39, J4.pin_3, J4.pin_10
  N3: J1.pin3, J1.pin38, J4.pin_4, J4.pin_9
  N4: J1.pin4, J1.pin37, J4.pin_5, J4.pin_8
  N5: J1.pin5, J1.pin36, J6.pin2, J6.pin_11
  N6: J1.pin6, J1.pin35, J6.pin_3, J6.pin_10
  N7: J1.pin7, J1.pin34, J6.pin_4, J6.pin_9
  N8: J1.pin8, J1.pin33, J6.pin_5, J6.pin_8
  N9: J1.pin9, J1.pin32, J7.pin2, J7.pin_11
  N10: J1.pin10, J1.pin31, J7.pin_3, J7.pin_10
  N11: J1.pin11, J1.pin30, J7.pin_4, J7.pin_9
  N12: J1.pin12, J1.pin29, J7.pin_5, J7.pin_8
  N13: J1.pin13, J1.pin28, J5.pin2, J5.pin_11
  N14: J1.pin14, J1.pin27, J5.pin_3, J5.pin_10
  N15: J1.pin15, J1.pin26, J5.pin_4, J5.pin_9
  N16: J1.pin16, J1.pin25, J5.pin_5, J5.pin_8
  N17: J1.pin17, J1.pin19, J1.pin21, J1.pin23, J5.pin_17, J6.pin_17, J7.pin_17, J4.pin_17, J2.pin2, J19.pin3, J19.pin28, J23.pin1, J23.pin2
  N18: J1.pin18, R1.Pin_1, J20.pin2
  N19: J1.pin20, R2.Pin_1, J20.pin29
  N20: J1.pin22, R3.Pin_1, J20.pin1
  N21: J1.pin24, R4.Pin_1, J20.pin30
  N22: J5.pin1, J5.pin_12, J6.pin1, J6.pin_12, J7.pin1, J7.pin_12, J4.pin1, J4.pin_12, J8.pin2, J12.pin5, J19.pin1, J19.pin30, J24.pin1, J24.pin2
  N23: J5.pin_15, J20.pin4
  N24: J5.pin_16, J20.pin3
  N25: J5.pin_18, J6.pin_18, J7.pin_18, J4.pin_18, J19.pin27
  N26: J5.pin_19, J6.pin_19, J7.pin_19, J4.pin_19, J19.pin26
  N27: J5.pin_20, J6.pin_20, J7.pin_20, J4.pin_20, J19.pin25
  N28: J6.pin_14, J7.pin_14
  N29: J6.pin_15, J7.pin_15, J20.pin6
  N30: J6.pin_16, J7.pin_16, J20.pin5
  N31: J4.pin_15, J17.pin2
  N32: J4.pin_16, J18.pin2
  N33: R3.Pin_0, R4.Pin_0
  N34: J2.pin3, J17.pin3, J12.pin1, J20.pin8
  N35: J2.pin4, J18.pin3, J12.pin2, J20.pin7
  N36: J2.pin5, J17.pin1, J12.pin3
  N37: J2.pin6, J18.pin1, J12.pin4
  N38: OMRON1.COIL1, D1.cathode
  N39: OMRON1.C, J10.pin1
  N40: OMRON1.COIL2, Q1.C, D1.anode
  N41: OMRON1.B, J10.pin2
  N42: Q1.B, R5.Pin_0
  N43: R5.Pin_1, J20.pin9
  N44: J19.pin2, J19.pin29

notes:
  X
  Y2
  Y1
  Z
  24v In
  Machine Connection
  Arduino
  Torch Height Control
  -
  +
  GND
  EN/CS
  STEP
  DIR
  +VCC
  +VMOT
  Driver
  2211
  D ->
  S ->
  D <-
  S <-
  Miso
  Mosi
  SCK
  THC Bypass
  S
  D
  1
  0
  Connector 1
  Connector 2
  24v
  gnd
  Buck Converter
  Fire Relay
  out -
  out +
  IN-
  IN+
  Torch

custom parts:
  Generic female header - 2 pins: Generic female header
