# Fritzing sketch thc board (saved by Fritzing 0.9.3b)
circuit board: 10cm x 5.52822cm
breadboards: 1

parts:
  Part1 = Arduino Nano (Rev3.0)
  J2 = Camdenboss CTB0158-4 [part_number=CTB0158-4 package=THT]
  OMRON3 = OMRON PCB Power Relay – G5LE [part_number="G5LE-1\n" package=THT]
  OMRON2 = OMRON PCB Power Relay – G5LE [part_number="G5LE-1\n" package=THT]
  J3 = shrouded pin header, 10 pins [form="♂ (shrouded male)"]
  J4 = shrouded pin header, 10 pins [form="♂ (shrouded male)"]
  OMRON1 = OMRON PCB Power Relay – G5LE [part_number="G5LE-1\n" package=THT]
  Part2 = Arduino Mega 2560 (Rev3)
  R1 = Resistor [tolerance=±5% resistance=220 package=THT]
  Q1 = NPN-Transistor [package="TO92 [THT]"]
  U1 = DIODE-ZENER [package=diode-zener]
  U2 = DIODE-ZENER [package=diode-zener]
  U3 = DIODE-ZENER [package=diode-zener]
  R2 = Resistor [tolerance=±5% resistance=220 package=THT]
  Q2 = NPN-Transistor [package="TO92 [THT]"]
  R3 = Resistor [tolerance=±5% resistance=220 package=THT]
  Q3 = NPN-Transistor [package="TO92 [THT]"]
  J1 = shrouded pin header, 10 pins [form="♂ (shrouded male)"]

nets:
  N1: Part1.D1/TX, J1.pin8
  N2: Part1.D0/RX, J1.pin9
  N3: Part1.D3, R2.Pin_0
  N4: Part1.D4, R1.Pin_0
  N5: Part1.D6, J1.pin10
  N6: Part1.D7, Part2.D10_PWM
  N7: Part1.D8, OMRON3.A
  N8: Part1.D9, OMRON2.A
  5V: Part1.5V, OMRON3.COIL1, OMRON2.COIL1, J3.pin6, OMRON1.COIL1, Part2.5V, U1.C, U2.C, U3.C, J1.pin2
  N9: Part1.A5, Part2.D21/SCL
  N10: Part1.A4, Part2.D20/SDA
  N11: Part1.A0, J2.pin4, Part2.A0
  N12: J2.pin1, OMRON1.A
  N13: J2.pin2, OMRON1.C
  N14: OMRON3.C, J1.pin6
  N15: OMRON3.COIL2, U1.A, Q2.C
  N16: OMRON3.B, J1.pin4
  N17: OMRON2.C, J1.pin5
  N18: OMRON2.COIL2, Q1.C, U2.A
  N19: OMRON2.B, J1.pin3
  N20: J3.pin2, Part2.D50
  N21: J3.pin3, Part2.D48
  N22: J3.pin5, Part2.GND
  N23: J3.pin9, Part2.D53
  N24: J3.pin10, Part2.D52
  N25: J4.pin2, Part2.D32
  N26: J4.pin3, Part2.D30
  N27: OMRON1.COIL2, U3.A, Q3.C
  N28: R1.Pin_1, Q1.B
  N29: R2.Pin_1, Q2.B
  N30: R3.Pin_0, J1.pin7
  N31: R3.Pin_1, Q3.B

notes:
  ARC -
  ARC +
  Fire 2
  Fire 1
  Step
  Dir
  Arduino Nano
  1
  2
  Plasma Torch Height Control
  To Main Board
  Rev 1.0
  Torch
  Relay
  Screw Terminal
  <-- USB Side
